// Logisim project DMUX4Way.circ as structural Verilog: 1 circuit, main circuit main
module main (
  input  in_1,
  input  in_2,
  input  in_3,
  output out_4,
  output out_5,
  output out_6,
  output out_7
);

  wire demultiplexer_1_out0, demultiplexer_1_out1;

  Demultiplexer demultiplexer_1 (.out0(demultiplexer_1_out0), .out1(demultiplexer_1_out1), .in(in_1), .sel(in_2));
  Demultiplexer demultiplexer_2 (.out0(out_4), .out1(out_5), .in(demultiplexer_1_out0), .sel(in_3));
  Demultiplexer demultiplexer_3 (.out0(out_6), .out1(out_7), .in(demultiplexer_1_out1), .sel(in_3));
endmodule
