// Logisim project DMUX8Way.circ as structural Verilog: 1 circuit, main circuit main
module main (
  input  in_1,
  input  in_2,
  input  [1:0] in_3,
  output out_4,
  output out_5,
  output out_6,
  output out_7,
  output out_8,
  output out_9,
  output out_10,
  output out_11
);

  wire demultiplexer_1_out0, demultiplexer_1_out1;

  Demultiplexer demultiplexer_1 (.out0(demultiplexer_1_out0), .out1(demultiplexer_1_out1), .in(in_1), .sel(in_2));
  Demultiplexer #(.select(2)) demultiplexer_2 (
    .out0(out_4), .out1(out_5), .out2(out_6), .out3(out_7), .in(demultiplexer_1_out0), .sel(in_3));
  Demultiplexer #(.select(2)) demultiplexer_3 (
    .out0(out_8), .out1(out_9), .out2(out_10), .out3(out_11), .in(demultiplexer_1_out1), .sel(in_3));
endmodule
