// Logisim project MUX16.circ as structural Verilog: 1 circuit, main circuit main
module main (
  input  in_1,
  input  in_2,
  input  in_3,
  input  in_4,
  input  in_5,
  input  in_6,
  input  in_7,
  input  in_8,
  input  in_9,
  input  in_10,
  input  in_11,
  input  in_12,
  input  in_13,
  input  in_14,
  input  in_15,
  input  in_16,
  input  in_17,
  input  in_18,
  input  in_19,
  input  in_20,
  input  in_21,
  input  in_22,
  input  in_23,
  input  in_24,
  input  in_25,
  input  in_26,
  input  in_27,
  input  in_28,
  input  in_29,
  input  in_30,
  input  in_31,
  input  in_32,
  input  in_33,
  output out_34,
  output out_35,
  output out_36,
  output out_37,
  output out_38,
  output out_39,
  output out_40,
  output out_41,
  output out_42,
  output out_43,
  output out_44,
  output out_45,
  output out_46,
  output out_47,
  output out_48,
  output out_49
);

  Multiplexer multiplexer_1 (.in0(in_1), .in1(in_2), .out(out_34), .sel(in_33));
  Multiplexer multiplexer_2 (.in0(in_3), .in1(in_4), .out(out_35), .sel(in_33));
  Multiplexer multiplexer_3 (.in0(in_5), .in1(in_6), .out(out_36), .sel(in_33));
  Multiplexer multiplexer_4 (.in0(in_7), .in1(in_8), .out(out_37), .sel(in_33));
  Multiplexer multiplexer_5 (.in0(in_9), .in1(in_10), .out(out_38), .sel(in_33));
  Multiplexer multiplexer_6 (.in0(in_11), .in1(in_12), .out(out_39), .sel(in_33));
  Multiplexer multiplexer_7 (.in0(in_13), .in1(in_14), .out(out_40), .sel(in_33));
  Multiplexer multiplexer_8 (.in0(in_15), .in1(in_16), .out(out_41), .sel(in_33));
  Multiplexer multiplexer_9 (.in0(in_17), .in1(in_18), .out(out_42), .sel(in_33));
  Multiplexer multiplexer_10 (.in0(in_19), .in1(in_20), .out(out_43), .sel(in_33));
  Multiplexer multiplexer_11 (.in0(in_21), .in1(in_22), .out(out_44), .sel(in_33));
  Multiplexer multiplexer_12 (.in0(in_23), .in1(in_24), .out(out_45), .sel(in_33));
  Multiplexer multiplexer_13 (.in0(in_25), .in1(in_26), .out(out_46), .sel(in_33));
  Multiplexer multiplexer_14 (.in0(in_27), .in1(in_28), .out(out_47), .sel(in_33));
  Multiplexer multiplexer_15 (.in0(in_29), .in1(in_30), .out(out_48), .sel(in_33));
  Multiplexer multiplexer_16 (.in0(in_31), .in1(in_32), .out(out_49), .sel(in_33));
endmodule
