// Logisim project MUX8Way16.circ as structural Verilog: 1 circuit, main circuit main
module main (
  input  [15:0] in_1,
  input  [15:0] in_2,
  input  [15:0] in_3,
  input  [15:0] in_4,
  input  [15:0] in_5,
  input  [15:0] in_6,
  input  [15:0] in_7,
  input  [15:0] in_8,
  input  [1:0] in_9,
  input  in_10,
  output [15:0] out_11
);

  wire [15:0] multiplexer_1_out, multiplexer_2_out;

  Multiplexer #(.select(2), .width(16)) multiplexer_1 (
    .in0(in_1), .in1(in_2), .in2(in_3), .in3(in_4), .out(multiplexer_1_out), .sel(in_9));
  Multiplexer #(.select(2), .width(16)) multiplexer_2 (
    .in0(in_5), .in1(in_6), .in2(in_7), .in3(in_8), .out(multiplexer_2_out), .sel(in_9));
  Multiplexer #(.width(16)) multiplexer_3 (.in0(multiplexer_1_out), .in1(multiplexer_2_out), .out(out_11), .sel(in_10));
endmodule
