// Logisim project OR16.circ as structural Verilog: 1 circuit, main circuit main
module main (
  input  in_1,
  input  in_2,
  input  in_3,
  input  in_4,
  input  in_5,
  input  in_6,
  input  in_7,
  input  in_8,
  input  in_9,
  input  in_10,
  input  in_11,
  input  in_12,
  input  in_13,
  input  in_14,
  input  in_15,
  input  in_16,
  input  in_17,
  input  in_18,
  input  in_19,
  input  in_20,
  input  in_21,
  input  in_22,
  input  in_23,
  input  in_24,
  input  in_25,
  input  in_26,
  input  in_27,
  input  in_28,
  input  in_29,
  input  in_30,
  input  in_31,
  input  in_32,
  output out_33,
  output out_34,
  output out_35,
  output out_36,
  output out_37,
  output out_38,
  output out_39,
  output out_40,
  output out_41,
  output out_42,
  output out_43,
  output out_44,
  output out_45,
  output out_46,
  output out_47,
  output out_48
);

  or or_1 (out_33, in_1, in_2);
  or or_2 (out_34, in_3, in_4);
  or or_3 (out_35, in_5, in_6);
  or or_4 (out_36, in_7, in_8);
  or or_5 (out_37, in_9, in_10);
  or or_6 (out_38, in_11, in_12);
  or or_7 (out_39, in_13, in_14);
  or or_8 (out_40, in_15, in_16);
  or or_9 (out_41, in_17, in_18);
  or or_10 (out_42, in_19, in_20);
  or or_11 (out_43, in_21, in_22);
  or or_12 (out_44, in_23, in_24);
  or or_13 (out_45, in_25, in_26);
  or or_14 (out_46, in_27, in_28);
  or or_15 (out_47, in_29, in_30);
  or or_16 (out_48, in_31, in_32);
endmodule
