// Logisim project ALU.circ as structural Verilog: 3 circuits, main circuit NegatorCustom
module NegatorCustom (
  input  [15:0] in_1,
  output [15:0] out_2
);

  wire [15:0] not_1_out;

  assign not_1_out = ~in_1;  // NOT_Gate not_1, 16 bits wide
  Inc16 inc16_1 (.in_1(not_1_out), .out_2(out_2));
endmodule

module Inc16 (
  input  [15:0] in_1,
  output [15:0] out_2
);

  Adder #(.width(16)) adder_1 (.a(in_1), .b(16'h1), .out(out_2));  // open: cin, cout
endmodule

module ALU (
  input  zx,
  input  nx,
  input  f,
  input  no,
  input  [15:0] x,
  input  zy,
  input  ny,
  input  [15:0] y,
  output [15:0] main_out,
  output zr,
  output ng
);

  wire [15:0] adder_1_out, and_1_out, multiplexer_1_out, multiplexer_2_out, multiplexer_3_out, not_1_out,
       not_2_out, not_3_out, not_4_out, not_5_out, not_6_out, xor_1_out;

  assign not_1_out = ~{16{1'b0}};  // NOT_Gate not_1, 16 bits wide
  assign not_2_out = ~{16{1'b0}};  // NOT_Gate not_2, 16 bits wide
  assign not_3_out = ~x;  // NOT_Gate not_3, 16 bits wide
  assign not_4_out = ~y;  // NOT_Gate not_4, 16 bits wide
  Multiplexer #(.select(2), .width(16)) multiplexer_1 (
    .in0(x), .in1(not_3_out), .in2({16{1'b0}}), .in3(not_1_out), .out(multiplexer_1_out), .sel({zx, nx}));
  Multiplexer #(.select(2), .width(16)) multiplexer_2 (
    .in0(y), .in1(not_4_out), .in2({16{1'b0}}), .in3(not_2_out), .out(multiplexer_2_out), .sel({zy, ny}));
  // Probe on multiplexer_1_out
  // Probe on multiplexer_2_out
  assign and_1_out = multiplexer_1_out & multiplexer_2_out;  // AND_Gate and_1, 16 bits wide
  Adder #(.width(16)) adder_1 (.a(multiplexer_1_out), .b(multiplexer_2_out), .out(adder_1_out));  // open: cin, cout
  Multiplexer #(.width(16)) multiplexer_3 (.in0(and_1_out), .in1(adder_1_out), .out(multiplexer_3_out), .sel(f));
  // Probe on multiplexer_3_out
  assign not_5_out = ~multiplexer_3_out;  // NOT_Gate not_5, 16 bits wide
  Multiplexer #(.width(16)) multiplexer_4 (.in0(multiplexer_3_out), .in1(not_5_out), .out(main_out), .sel(no));
  assign xor_1_out = main_out ^ {16{1'b0}};  // XOR_Gate xor_1, 16 bits wide
  assign not_6_out = ~xor_1_out;  // NOT_Gate not_6, 16 bits wide
  and and_2 (zr, not_6_out[0], not_6_out[1], not_6_out[2], not_6_out[3], not_6_out[4], not_6_out[5], not_6_out[6], not_6_out[7], not_6_out[8], not_6_out[9], not_6_out[10], not_6_out[11], not_6_out[12], not_6_out[13], not_6_out[14], not_6_out[15]);

  assign ng = main_out[15];
endmodule
