// Logisim project FullAdder.circ as structural Verilog: 2 circuits, main circuit HalfAdder
module HalfAdder (
  input  a,
  input  b,
  output c,
  output s
);

  and and_1 (c, a, b);
  xor xor_1 (s, a, b);
endmodule

module FullAdder (
  input  a,
  input  b,
  input  c,
  output carry,
  output sum
);

  wire halfadder_1_c, halfadder_1_s, halfadder_2_c;

  HalfAdder halfadder_1 (.a(a), .b(b), .c(halfadder_1_c), .s(halfadder_1_s));
  HalfAdder halfadder_2 (.a(halfadder_1_s), .b(c), .c(halfadder_2_c), .s(sum));
  or or_1 (carry, halfadder_1_c, halfadder_2_c);
endmodule
