// Logisim project HalfAdder.circ as structural Verilog: 2 circuits, main circuit main
module main (
  input  a,
  input  b,
  output c,
  output s
);

  and and_1 (c, a, b);
  xor xor_1 (s, a, b);
endmodule

module HalfAdder (
  input  a,
  input  b,
  output c,
  output s
);

  and and_1 (c, a, b);
  xor xor_1 (s, a, b);
endmodule
