// Logisim project Inc16.circ as structural Verilog: 1 circuit, main circuit Inc16
module Inc16 (
  input  [15:0] in_1,
  output [15:0] out_2
);

  Adder #(.width(16)) adder_1 (.a(in_1), .b(16'h1), .out(out_2));  // open: cin, cout
endmodule
