// Logisim project add16.circ as structural Verilog: 3 circuits, main circuit main
module main (
  input  in_1,
  input  in_2,
  input  in_3,
  input  in_4,
  input  in_5,
  input  in_6,
  input  in_7,
  input  in_8,
  input  in_9,
  input  in_10,
  input  in_11,
  input  in_12,
  input  in_13,
  input  in_14,
  input  in_15,
  input  in_16,
  input  in_17,
  input  in_18,
  input  in_19,
  input  in_20,
  input  in_21,
  input  in_22,
  input  in_23,
  input  in_24,
  input  in_25,
  input  in_26,
  input  in_27,
  input  in_28,
  input  in_29,
  input  in_30,
  input  in_31,
  input  in_32,
  output out_33,
  output out_34,
  output out_35,
  output out_36,
  output out_37,
  output out_38,
  output out_39,
  output out_40,
  output out_41,
  output out_42,
  output out_43,
  output out_44,
  output out_45,
  output out_46,
  output out_47,
  output out_48
);

  wire fulladder_1_carry, fulladder_2_carry, fulladder_3_carry, fulladder_4_carry, fulladder_5_carry,
       fulladder_6_carry, fulladder_7_carry, fulladder_8_carry, fulladder_9_carry, fulladder_10_carry,
       fulladder_11_carry, fulladder_12_carry, fulladder_13_carry, fulladder_14_carry, halfadder_1_c,
       xor_1_out;

  HalfAdder halfadder_1 (.a(in_1), .b(in_2), .c(halfadder_1_c), .s(out_33));
  FullAdder fulladder_1 (.a(in_3), .b(in_4), .c(halfadder_1_c), .carry(fulladder_1_carry), .sum(out_34));
  FullAdder fulladder_2 (.a(in_5), .b(in_6), .c(fulladder_1_carry), .carry(fulladder_2_carry), .sum(out_35));
  FullAdder fulladder_3 (.a(in_7), .b(in_8), .c(fulladder_2_carry), .carry(fulladder_3_carry), .sum(out_36));
  FullAdder fulladder_4 (.a(in_9), .b(in_10), .c(fulladder_3_carry), .carry(fulladder_4_carry), .sum(out_37));
  FullAdder fulladder_5 (.a(in_11), .b(in_12), .c(fulladder_4_carry), .carry(fulladder_5_carry), .sum(out_38));
  FullAdder fulladder_6 (.a(in_13), .b(in_14), .c(fulladder_5_carry), .carry(fulladder_6_carry), .sum(out_39));
  FullAdder fulladder_7 (.a(in_15), .b(in_16), .c(fulladder_6_carry), .carry(fulladder_7_carry), .sum(out_40));
  FullAdder fulladder_8 (.a(in_17), .b(in_18), .c(fulladder_7_carry), .carry(fulladder_8_carry), .sum(out_41));
  FullAdder fulladder_9 (.a(in_19), .b(in_20), .c(fulladder_8_carry), .carry(fulladder_9_carry), .sum(out_42));
  FullAdder fulladder_10 (.a(in_21), .b(in_22), .c(fulladder_9_carry), .carry(fulladder_10_carry), .sum(out_43));
  FullAdder fulladder_11 (.a(in_23), .b(in_24), .c(fulladder_10_carry), .carry(fulladder_11_carry), .sum(out_44));
  FullAdder fulladder_12 (.a(in_25), .b(in_26), .c(fulladder_11_carry), .carry(fulladder_12_carry), .sum(out_45));
  FullAdder fulladder_13 (.a(in_27), .b(in_28), .c(fulladder_12_carry), .carry(fulladder_13_carry), .sum(out_46));
  FullAdder fulladder_14 (.a(in_29), .b(in_30), .c(fulladder_13_carry), .carry(fulladder_14_carry), .sum(out_47));
  xor xor_1 (xor_1_out, fulladder_14_carry, in_31);
  xor xor_2 (out_48, xor_1_out, in_32);
endmodule

module HalfAdder (
  input  a,
  input  b,
  output c,
  output s
);

  and and_1 (c, a, b);
  xor xor_1 (s, a, b);
endmodule

module FullAdder (
  input  a,
  input  b,
  input  c,
  output carry,
  output sum
);

  wire halfadder_1_c, halfadder_1_s, halfadder_2_c;

  HalfAdder halfadder_1 (.a(a), .b(b), .c(halfadder_1_c), .s(halfadder_1_s));
  HalfAdder halfadder_2 (.a(halfadder_1_s), .b(c), .c(halfadder_2_c), .s(sum));
  or or_1 (carry, halfadder_1_c, halfadder_2_c);
endmodule
