// Logisim project BeautifulRam512.circ as structural Verilog: 1 circuit, main circuit main
module main (
  input  [15:0] in_1,
  input  [8:0] in_2,
  input  in_3,
  output [15:0] out_4
);

  wire clock_1_out, clock_2_out, clock_3_out, clock_4_out, clock_5_out, clock_6_out, clock_7_out,
       clock_8_out, demultiplexer_1_out0, demultiplexer_1_out1, demultiplexer_1_out2, demultiplexer_1_out3,
       demultiplexer_1_out4, demultiplexer_1_out5, demultiplexer_1_out6, demultiplexer_1_out7;
  wire [15:0] ram_1_dout, ram_2_dout, ram_3_dout, ram_4_dout, ram_5_dout, ram_6_dout, ram_7_dout, ram_8_dout;

  Demultiplexer #(.select(3)) demultiplexer_1 (
    .out0(demultiplexer_1_out0), .out1(demultiplexer_1_out1), .out2(demultiplexer_1_out2),
    .out3(demultiplexer_1_out3), .out4(demultiplexer_1_out4), .out5(demultiplexer_1_out5),
    .out6(demultiplexer_1_out6), .out7(demultiplexer_1_out7), .in(in_3), .sel(in_2[8:6]));
  RAM #(.addrWidth(6), .dataWidth(16), .enables("line")) ram_1 (
    .addr(in_2[5:0]), .we(demultiplexer_1_out0), .clk(clock_1_out), .din(in_1), .dout(ram_1_dout));
  Clock clock_1 (.out(clock_1_out));
  RAM #(.addrWidth(6), .dataWidth(16), .enables("line")) ram_2 (
    .addr(in_2[5:0]), .we(demultiplexer_1_out1), .clk(clock_2_out), .din(in_1), .dout(ram_2_dout));
  Clock clock_2 (.out(clock_2_out));
  RAM #(.addrWidth(6), .dataWidth(16), .enables("line")) ram_3 (
    .addr(in_2[5:0]), .we(demultiplexer_1_out2), .clk(clock_3_out), .din(in_1), .dout(ram_3_dout));
  Clock clock_3 (.out(clock_3_out));
  RAM #(.addrWidth(6), .dataWidth(16), .enables("line")) ram_4 (
    .addr(in_2[5:0]), .we(demultiplexer_1_out3), .clk(clock_4_out), .din(in_1), .dout(ram_4_dout));
  Clock clock_4 (.out(clock_4_out));
  RAM #(.addrWidth(6), .dataWidth(16), .enables("line")) ram_5 (
    .addr(in_2[5:0]), .we(demultiplexer_1_out4), .clk(clock_5_out), .din(in_1), .dout(ram_5_dout));
  Clock clock_5 (.out(clock_5_out));
  RAM #(.addrWidth(6), .dataWidth(16), .enables("line")) ram_6 (
    .addr(in_2[5:0]), .we(demultiplexer_1_out5), .clk(clock_6_out), .din(in_1), .dout(ram_6_dout));
  Clock clock_6 (.out(clock_6_out));
  RAM #(.addrWidth(6), .dataWidth(16), .enables("line")) ram_7 (
    .addr(in_2[5:0]), .we(demultiplexer_1_out6), .clk(clock_7_out), .din(in_1), .dout(ram_7_dout));
  Clock clock_7 (.out(clock_7_out));
  RAM #(.addrWidth(6), .dataWidth(16), .enables("line")) ram_8 (
    .addr(in_2[5:0]), .we(demultiplexer_1_out7), .clk(clock_8_out), .din(in_1), .dout(ram_8_dout));
  Clock clock_8 (.out(clock_8_out));
  Multiplexer #(.select(3), .width(16)) multiplexer_1 (
    .in0(ram_1_dout), .in1(ram_2_dout), .in2(ram_3_dout), .in3(ram_4_dout), .in4(ram_5_dout),
    .in5(ram_6_dout), .in6(ram_7_dout), .in7(ram_8_dout), .out(out_4), .sel(in_2[8:6]));
endmodule
