// Logisim project DownloadMoreRam16k.circ as structural Verilog: 1 circuit, main circuit main
module main (
  input  [13:0] in_1,
  input  [15:0] in_2,
  input  in_3,
  output [15:0] out_4
);

  wire clock_1_out, demultiplexer_1_out0, demultiplexer_1_out1, demultiplexer_1_out2, demultiplexer_1_out3;
  wire [15:0] ram_1_dout, ram_2_dout, ram_3_dout, ram_4_dout;

  Clock clock_1 (.out(clock_1_out));
  Demultiplexer #(.select(2)) demultiplexer_1 (
    .out0(demultiplexer_1_out0), .out1(demultiplexer_1_out1), .out2(demultiplexer_1_out2),
    .out3(demultiplexer_1_out3), .in(in_3), .sel(in_1[13:12]));
  RAM #(.addrWidth(12), .dataWidth(16), .enables("line")) ram_1 (
    .addr(in_1[11:0]), .we(demultiplexer_1_out0), .clk(clock_1_out), .din(in_2), .dout(ram_1_dout));
  RAM #(.addrWidth(12), .dataWidth(16), .enables("line")) ram_2 (
    .addr(in_1[11:0]), .we(demultiplexer_1_out1), .clk(clock_1_out), .din(in_2), .dout(ram_2_dout));
  RAM #(.addrWidth(12), .dataWidth(16), .enables("line")) ram_3 (
    .addr(in_1[11:0]), .we(demultiplexer_1_out2), .clk(clock_1_out), .din(in_2), .dout(ram_3_dout));
  RAM #(.addrWidth(12), .dataWidth(16), .enables("line")) ram_4 (
    .addr(in_1[11:0]), .we(demultiplexer_1_out3), .clk(clock_1_out), .din(in_2), .dout(ram_4_dout));
  Multiplexer #(.select(2), .width(16)) multiplexer_1 (
    .in0(ram_1_dout), .in1(ram_2_dout), .in2(ram_3_dout), .in3(ram_4_dout), .out(out_4), .sel(in_1[13:12]));
endmodule
