// Logisim project MyRegister.circ as structural Verilog: 1 circuit, main circuit main
module main (
  input  in_1,
  input  in_2,
  input  in_3,
  input  in_4,
  input  in_5,
  input  in_6,
  input  in_7,
  input  in_8,
  input  in_9,
  input  in_10,
  input  in_11,
  input  in_12,
  input  in_13,
  input  in_14,
  input  in_15,
  input  in_16,
  input  in_17,
  output out_18,
  output out_19,
  output out_20,
  output out_21,
  output out_22,
  output out_23,
  output out_24,
  output out_25,
  output out_26,
  output out_27,
  output out_28,
  output out_29,
  output out_30,
  output out_31,
  output out_32,
  output out_33
);

  wire clock_1_out, clock_2_out, clock_3_out, clock_4_out, clock_5_out, clock_6_out, clock_7_out,
       clock_8_out, clock_9_out, clock_10_out, clock_11_out, clock_12_out, clock_13_out, clock_14_out,
       clock_15_out, clock_16_out;

  Register #(.width(1)) register_1 (.D(in_1), .en(in_2), .clk(clock_1_out), .Q(out_18));  // open: clr
  Clock clock_1 (.out(clock_1_out));
  Register #(.width(1)) register_2 (.D(in_3), .en(in_2), .clk(clock_2_out), .Q(out_19));  // open: clr
  Clock clock_2 (.out(clock_2_out));
  Register #(.width(1)) register_3 (.D(in_4), .en(in_2), .clk(clock_3_out), .Q(out_20));  // open: clr
  Clock clock_3 (.out(clock_3_out));
  Register #(.width(1)) register_4 (.D(in_5), .en(in_2), .clk(clock_4_out), .Q(out_21));  // open: clr
  Clock clock_4 (.out(clock_4_out));
  Register #(.width(1)) register_5 (.D(in_6), .en(in_2), .clk(clock_5_out), .Q(out_22));  // open: clr
  Clock clock_5 (.out(clock_5_out));
  Register #(.width(1)) register_6 (.D(in_7), .en(in_2), .clk(clock_6_out), .Q(out_23));  // open: clr
  Clock clock_6 (.out(clock_6_out));
  Register #(.width(1)) register_7 (.D(in_8), .en(in_2), .clk(clock_7_out), .Q(out_24));  // open: clr
  Clock clock_7 (.out(clock_7_out));
  Register #(.width(1)) register_8 (.D(in_9), .en(in_2), .clk(clock_8_out), .Q(out_25));  // open: clr
  Clock clock_8 (.out(clock_8_out));
  Register #(.width(1)) register_9 (.D(in_10), .en(in_2), .clk(clock_9_out), .Q(out_26));  // open: clr
  Clock clock_9 (.out(clock_9_out));
  Register #(.width(1)) register_10 (.D(in_11), .en(in_2), .clk(clock_10_out), .Q(out_27));  // open: clr
  Clock clock_10 (.out(clock_10_out));
  Register #(.width(1)) register_11 (.D(in_12), .en(in_2), .clk(clock_11_out), .Q(out_28));  // open: clr
  Clock clock_11 (.out(clock_11_out));
  Register #(.width(1)) register_12 (.D(in_13), .en(in_2), .clk(clock_12_out), .Q(out_29));  // open: clr
  Clock clock_12 (.out(clock_12_out));
  Register #(.width(1)) register_13 (.D(in_14), .en(in_2), .clk(clock_13_out), .Q(out_30));  // open: clr
  Clock clock_13 (.out(clock_13_out));
  Register #(.width(1)) register_14 (.D(in_15), .en(in_2), .clk(clock_14_out), .Q(out_31));  // open: clr
  Clock clock_14 (.out(clock_14_out));
  Register #(.width(1)) register_15 (.D(in_16), .en(in_2), .clk(clock_15_out), .Q(out_32));  // open: clr
  Clock clock_15 (.out(clock_15_out));
  Register #(.width(1)) register_16 (.D(in_17), .en(in_2), .clk(clock_16_out), .Q(out_33));  // open: clr
  Clock clock_16 (.out(clock_16_out));
endmodule
