// Logisim project PC.circ as structural Verilog: 1 circuit, main circuit main
module main (
  input  [15:0] chip_in,
  input  inc,
  input  load,
  input  reset,
  output [15:0] chip_out
);

  wire clock_1_out;
  wire [15:0] adder_1_out, multiplexer_1_out;

  // Probe on {reset, load, inc}
  Multiplexer #(.select(3), .width(16)) multiplexer_1 (
    .in0(chip_out), .in1(adder_1_out), .in2(chip_in), .in3(chip_in), .in4({16{1'b0}}), .in5({16{1'b0}}),
    .in6({16{1'b0}}), .in7({16{1'b0}}), .out(multiplexer_1_out), .sel({reset, load, inc}));
  Register #(.width(16)) register_1 (.D(multiplexer_1_out), .en(1'b1), .clk(clock_1_out), .Q(chip_out));  // open: clr
  Clock clock_1 (.out(clock_1_out));
  Adder #(.width(16)) adder_1 (.a(16'h1), .b(chip_out), .out(adder_1_out));  // open: cin, cout
endmodule
