// Logisim project Perfect_Ram_4k.circ as structural Verilog: 1 circuit, main circuit main
module main (
  input  [11:0] in_1,
  input  [15:0] in_2,
  input  in_3,
  output [15:0] out_4
);

  wire clock_1_out, demultiplexer_1_out0, demultiplexer_1_out1, demultiplexer_1_out2, demultiplexer_1_out3,
       demultiplexer_1_out4, demultiplexer_1_out5, demultiplexer_1_out6, demultiplexer_1_out7;
  wire [15:0] ram_1_dout, ram_2_dout, ram_3_dout, ram_4_dout, ram_5_dout, ram_6_dout, ram_7_dout, ram_8_dout;

  Clock clock_1 (.out(clock_1_out));
  Demultiplexer #(.select(3)) demultiplexer_1 (
    .out0(demultiplexer_1_out0), .out1(demultiplexer_1_out1), .out2(demultiplexer_1_out2),
    .out3(demultiplexer_1_out3), .out4(demultiplexer_1_out4), .out5(demultiplexer_1_out5),
    .out6(demultiplexer_1_out6), .out7(demultiplexer_1_out7), .in(in_3), .sel(in_1[11:9]));
  RAM #(.addrWidth(9), .dataWidth(16), .enables("line")) ram_1 (
    .addr(in_1[8:0]), .we(demultiplexer_1_out0), .clk(clock_1_out), .din(in_2), .dout(ram_1_dout));
  RAM #(.addrWidth(9), .dataWidth(16), .enables("line")) ram_2 (
    .addr(in_1[8:0]), .we(demultiplexer_1_out1), .clk(clock_1_out), .din(in_2), .dout(ram_2_dout));
  RAM #(.addrWidth(9), .dataWidth(16), .enables("line")) ram_3 (
    .addr(in_1[8:0]), .we(demultiplexer_1_out2), .clk(clock_1_out), .din(in_2), .dout(ram_3_dout));
  RAM #(.addrWidth(9), .dataWidth(16), .enables("line")) ram_4 (
    .addr(in_1[8:0]), .we(demultiplexer_1_out3), .clk(clock_1_out), .din(in_2), .dout(ram_4_dout));
  RAM #(.addrWidth(9), .dataWidth(16), .enables("line")) ram_5 (
    .addr(in_1[8:0]), .we(demultiplexer_1_out4), .clk(clock_1_out), .din(in_2), .dout(ram_5_dout));
  RAM #(.addrWidth(9), .dataWidth(16), .enables("line")) ram_6 (
    .addr(in_1[8:0]), .we(demultiplexer_1_out5), .clk(clock_1_out), .din(in_2), .dout(ram_6_dout));
  RAM #(.addrWidth(9), .dataWidth(16), .enables("line")) ram_7 (
    .addr(in_1[8:0]), .we(demultiplexer_1_out6), .clk(clock_1_out), .din(in_2), .dout(ram_7_dout));
  RAM #(.addrWidth(9), .dataWidth(16), .enables("line")) ram_8 (
    .addr(in_1[8:0]), .we(demultiplexer_1_out7), .clk(clock_1_out), .din(in_2), .dout(ram_8_dout));
  Multiplexer #(.select(3), .width(16)) multiplexer_1 (
    .in0(ram_1_dout), .in1(ram_2_dout), .in2(ram_3_dout), .in3(ram_4_dout), .in4(ram_5_dout),
    .in5(ram_6_dout), .in6(ram_7_dout), .in7(ram_8_dout), .out(out_4), .sel(in_1[11:9]));
endmodule
