// Logisim project Program_Counter.circ as structural Verilog: 1 circuit, main circuit main
module main (
  input  inc,
  input  load,
  input  reset,
  input  [15:0] inp
);

  wire and_1_out, clock_1_out, not_1_out, not_2_out, not_3_out, not_4_out, not_5_out, or_1_out;
  wire [1:0] and_2_out;
  wire [15:0] adder_1_out, multiplexer_1_out, register_1_q;

  not not_1 (not_1_out, inc);
  not not_2 (not_2_out, load);
  Adder #(.width(16)) adder_1 (.a(16'h1), .b(register_1_q), .out(adder_1_out));  // open: cin, cout
  and and_1 (and_1_out, not_1_out, not_2_out);
  or or_1 (or_1_out, and_1_out, load);
  and and_2 (and_2_out[0], or_1_out, not_3_out);
  not not_3 (not_3_out, reset);
  not not_4 (not_4_out, load);
  and and_3 (and_2_out[1], not_4_out, not_5_out);
  not not_5 (not_5_out, reset);
  // Probe on and_2_out
  Multiplexer #(.select(2), .width(16)) multiplexer_1 (
    .in0({16{1'b0}}), .in1(inp), .in2(adder_1_out), .in3(register_1_q), .out(multiplexer_1_out),
    .sel(and_2_out));
  Register #(.width(16)) register_1 (
    .D(multiplexer_1_out), .en(1'b1), .clk(clock_1_out), .Q(register_1_q));  // open: clr
  Clock clock_1 (.out(clock_1_out));
endmodule
