// Logisim project bit.circ as structural Verilog: 1 circuit, main circuit main
module main (
  input  in_1,
  input  in_2,
  output out_3
);

  wire clock_1_out, multiplexer_1_out, not_1_out;

  Clock clock_1 (.out(clock_1_out));
  not not_1 (not_1_out, in_1);
  D_Flip_Flop d_ff_1 (.D(multiplexer_1_out), .clk(clock_1_out), .Q(out_3));  // open: Qn, preset, reset
  Multiplexer multiplexer_1 (.in0(in_2), .in1(out_3), .out(multiplexer_1_out), .sel(not_1_out));
endmodule
